# Fritzing sketch callboystimer (saved by Fritzing 0.9.6b)
breadboards: 1

parts:
  WeMos_D1_Mini1 = WeMos D1 Mini  # not connected
  LCD1 = LCD screen
  R1 = Trimmer Potentiometer [maximum_resistance=10kΩ package=THT]
  S1 = Pushbutton [package="[THT]"]
  Part1 = Adafruit MAX98357A I2S 3W Class D Amplifier [part_number="Adafruit #3006"]
  SP1 = SPEAKER [package=pcb_mount_speaker]
  R2 = Resistor [tolerance=±5% power=0.25 resistance=220 package=THT]
  R3 = Resistor [tolerance=±5% power=0.25 resistance=10k package=THT]

nets:
  VSS: LCD1.VSS, LCD1.DB5, R1.leg2, Part1.GND, R3.Pin_1
  N1: LCD1.VDD, R2.Pin_0
  N2: LCD1.DB7, R1.wiper
  N3: LCD1.LED+, R1.leg1, S1.Pin_1, S1.Pin_2, R2.Pin_1
  N4: S1.Pin_3, S1.Pin_4, R3.Pin_0
  N5: Part1.VO-, SP1.+
  N6: Part1.VO+, SP1.-

custom parts:
  Adafruit MAX98357A I2S 3W Class D Amplifier: Listen to this good news - we now have an all in one digital audio amp breakout board that works incredibly well with the Raspberry Pi! If you're looking for an easy and low cost way to get you digital sound files bumpin' then the MAX08357 I2S Amp Breakout is for you. It takes standard I2S digital audio input and, not only decodes it into analog, but also amplifies it directly into a speaker.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
